# Fritzing sketch diagram (saved by Fritzing 0.9.3b)
breadboards: 1

parts:
  Matrix_keypad1 = KEYPAD 4x4
  Part2 = Adafruit T-Cobbler Plus [part_number="Adafruit #1989 and #2028"]
  LCD2 = LCD screen
  LCM1602_IIC2 = LCM1602 IIC [part_number="LCM1602 IIC" chip_label="LCM1602 IIC" package="DIP (Dual Inline) [THT]"]
  PIR1 = PIR sensor
  J1 = Buzzer
  Part4 = Adafruit MiCS-5524 Gas Sensor [part_number="Adafruit #3199"]
  Part5 = Arduino Uno (Rev3)
  T1 = LM35 Temperature Sensor [package="TO92 [THT]"]

nets:
  N1: Matrix_keypad1.col1, Part2.GPIO4
  N2: Matrix_keypad1.col2, Part2.GPIO17
  N3: Matrix_keypad1.col3, Part2.GPIO27
  N4: Matrix_keypad1.col4, Part2.GPIO22
  N5: Matrix_keypad1.row1, Part2.GPIO18
  N6: Matrix_keypad1.row2, Part2.GPIO23
  N7: Matrix_keypad1.row3, Part2.GPIO24
  N8: Matrix_keypad1.row4, Part2.GPIO25
  +3.3V: Part2.+3.3V, PIR1.VDD
  N9: Part2.SDA, LCM1602_IIC2.SDA
  N10: Part2.SCL, LCM1602_IIC2.SCL
  GND: Part2.GND, LCM1602_IIC2.GND, PIR1.GND, J1.pin1
  N11: Part2.GPIO13, PIR1.SIG
  N12: Part2.GPIO26, Part4.ENABLE
  +5V: Part2.+5V, LCM1602_IIC2.VCC
  N13: Part2.GPIO21, J1.pin2
  VSS: LCD2.VSS, LCM1602_IIC2.VSS
  VDD: LCD2.VDD, LCM1602_IIC2.VDD
  N14: LCD2.V0, LCM1602_IIC2.V0
  N15: LCD2.RS, LCM1602_IIC2.RS
  N16: LCD2.R/W, LCM1602_IIC2.RW
  N17: LCD2.E, LCM1602_IIC2.E
  N18: LCD2.DB0, LCM1602_IIC2.D0
  N19: LCD2.DB1, LCM1602_IIC2.D1
  N20: LCD2.DB2, LCM1602_IIC2.D2
  N21: LCD2.DB3, LCM1602_IIC2.D3
  N22: LCD2.DB4, LCM1602_IIC2.D4
  N23: LCD2.DB5, LCM1602_IIC2.D5
  N24: LCD2.DB6, LCM1602_IIC2.D6
  N25: LCD2.DB7, LCM1602_IIC2.D7
  N26: LCD2.LED+, LCM1602_IIC2.A
  N27: LCD2.LED-, LCM1602_IIC2.K
  N28: LCM1602_IIC2.LED_A, LCM1602_IIC2.LED_B
  N29: Part4.5.0V, Part5.5V
  GND_2: Part4.GND, Part5.GND, T1.GND
  N30: Part4.AOUT, Part5.A0
  N31: Part5.A1, T1.Vout
  N32: Part5.N/C, T1.+Vs

custom parts:
  KEYPAD 4x4: Matrix keypad 16 buttons, 4 rows x 4 columns
  Adafruit T-Cobbler Plus: The Raspberry Pi has landed on the Maker World like a 40-GPIO pinned, quad-USB ported, credit card sized bomb of DIY joy. And while you can use most of our great Model B accessories by hooking up our downgrade cable, its probably a good time to upgrade your set up and accessorize using all of the 40 pins. That's why we now carry the Assembled Adafruit Pi T-Cobbler Plus - Breakout + Cable for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
  LCM1602 IIC: I2C-Module to use a 1602 or 2004 LCD on with the wire.h libory Serial LCD Modul
  Buzzer: Fixed frequency buzzer
  Adafruit MiCS-5524 Gas Sensor: Give your next sensor project a nose for gasses with the Adafruit MiCS-5524 Gas Sensor Breakout. This breakout makes it easy to use this nice sensor from SGX Sensortech. The MiCS-5524 is a robust MEMS sensor for indoor carbon monoxide and natural gas leakage detection, it's suitable also for indoor air quality monitoring; breath checker and early fire detection. Please note: This sensor is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
